// Logisim project parallel.circ as structural Verilog: 5 circuits, main circuit data_path
module data_path (
  input  clk,
  input  [7:0] number,
  input  multiply,
  input  load_C,
  input  carry_in,
  input  divide,
  input  load_B,
  input  invert,
  input  load_A,
  input  add,
  input  reset_result,
  output mult_ready,
  output [15:0] Result,
  output RR
);

  wire and_1_out, and_2_out, not_2_out, or_1_out, or_2_out, or_3_out, shift_register_1_p4,
       shift_register_1_p14, shift_register_1_p15, shift_register_1_p16, shift_register_1_p17,
       shift_register_1_p18, shift_register_1_p19, shift_register_1_p20, shift_register_2_p8,
       shift_register_2_p9, shift_register_2_p10;
  wire [7:0] controlled8inverter_1_f;
  wire [15:0] adder_1_out, from8to16_1_x16;

  // Shift_Register shift_register_1: pin names not known; wires that end beside it: load_B, multiply, clk, shift_register_1_p4, number[7], number[6], number[5], number[4], number[3], number[2], number[1], number[0], shift_register_1_p4, shift_register_1_p14, shift_register_1_p15, shift_register_1_p16, shift_register_1_p17, shift_register_1_p18, shift_register_1_p19, shift_register_1_p20
  // Shift_Register #(.length(3)) shift_register_2: pin names not known; wires that end beside it: load_C, divide, clk, 1'b0, 1'b0, number[2], number[1], shift_register_2_p8, shift_register_2_p9, shift_register_2_p10
  nor nor_1 (mult_ready, shift_register_1_p4, shift_register_1_p14, shift_register_1_p15, shift_register_1_p16, shift_register_1_p17, shift_register_1_p18, shift_register_1_p19, shift_register_1_p20);
  and and_1 (and_1_out, shift_register_1_p20, multiply);
  or or_1 (or_1_out, shift_register_2_p8, shift_register_2_p9, shift_register_2_p10);
  or or_2 (or_2_out, and_1_out, add);
  not not_1 (RR, or_1_out);
  and and_2 (and_2_out, or_1_out, divide);
  // Shift_Register #(.length(16)) shift_register_3: pin names not known; wires that end beside it: load_A, multiply, clk, 1'b0
  not not_2 (not_2_out, clk);
  // Shift_Register #(.length(16)) shift_register_4: pin names not known; wires that end beside it: reset_result, or_2_out, and_2_out, not_2_out, adder_1_out[15]
  or or_3 (or_3_out, carry_in, invert);
  Adder #(.width(16)) adder_1 (.a(from8to16_1_x16), .b(Result), .out(adder_1_out), .cin(or_3_out));  // open: cout
  from8to16 from8to16_1 (.x8(controlled8inverter_1_f), .x16(from8to16_1_x16));
  controlled8inverter controlled8inverter_1 (.invert(invert), .x(number), .f(controlled8inverter_1_f));
endmodule

module number_loader (
  input  clk,
  input  reset,
  input  [7:0] number,
  input  load_enable,
  input  [1:0] register_selector,
  output [7:0] x,
  output [7:0] y,
  output [7:0] z,
  output [7:0] t
);

  wire demultiplexer_1_out0, demultiplexer_1_out1, demultiplexer_1_out2, demultiplexer_1_out3;

  Demultiplexer #(.select(2)) demultiplexer_1 (
    .out0(demultiplexer_1_out0), .out1(demultiplexer_1_out1), .out2(demultiplexer_1_out2),
    .out3(demultiplexer_1_out3), .in(load_enable), .sel(register_selector));
  Register register_1 (.D(number), .en(demultiplexer_1_out0), .clk(clk), .Q(x), .clr(reset));
  Register register_2 (.D(number), .en(demultiplexer_1_out1), .clk(clk), .Q(y), .clr(reset));
  Register register_3 (.D(number), .en(demultiplexer_1_out2), .clk(clk), .Q(z), .clr(reset));
  Register register_4 (.D(number), .en(demultiplexer_1_out3), .clk(clk), .Q(t), .clr(reset));
endmodule

module from8to16 (
  input  [7:0] x8,
  output [15:0] x16
);


  assign x16 = {{9{x8[7]}}, x8[6:0]};
endmodule

module controlled8inverter (
  input  invert,
  input  [7:0] x,
  output [7:0] f
);

  xor xor_1 (f[7], invert, x[7]);
  xor xor_2 (f[6], invert, x[6]);
  xor xor_3 (f[5], invert, x[5]);
  xor xor_4 (f[4], invert, x[4]);
  xor xor_5 (f[3], invert, x[3]);
  xor xor_6 (f[2], invert, x[2]);
  xor xor_7 (f[1], invert, x[1]);
  xor xor_8 (f[0], invert, x[0]);
endmodule

module main (
);

  data_path data_path_1 ();  // open: clk, number, multiply, load_C, carry_in, divide, load_B, invert, load_A, add, reset_result, mult_ready, Result, RR
endmodule
